# Fritzing sketch Schematics (saved by Fritzing 0.9.2b)
breadboards: 1

parts:
  Raspberry_Pi1 = Raspberry Pi 2
  Part1 = Logic Level Converter
  IC1 = MCP3008 8-channel 10-bit ADC [part_number=MCP3008]  # not connected
  J1 = Piezo Speaker
  R1 = Resistor [tolerance=±5% resistance=1M package=THT]
  Part2 = ws2812b [package="smd 2812b"]
  Power_plug1 = Power plug
  JP1 = USB_MICROB_PLUG [package=micro-b-ra-th]

nets:
  N1: Raspberry_Pi1.GPIO18, Part1.TX_LV
  GND: Raspberry_Pi1.GND, Part1.GND, J1.pin1, R1.Pin_1, Part2.VSS, Power_plug1.GND, JP1.GND
  N2: Raspberry_Pi1.5V, Part1.HV
  N3: Part1.TX_HV, Part2.DIN
  N4: J1.pin2, R1.Pin_0
  VCC: Part2.VDD, Power_plug1.VCC, JP1.VCC
